# Fritzing sketch esp32+level-converter (saved by Fritzing 0.9.2b)
circuit board: 7cm x 5cm
breadboards: 2

parts:
  U1 = ESP32-38PinWide [part_number=ESP32-38PinWide]
  Part1 = Logic Level Converter
  Part2 = Logic Level Converter

nets:
  N1: U1.3.3, Part1.LV, Part2.LV
  N2: U1.GPIO32, Part2.RX2_LV
  N3: U1.GPIO33, Part2.TX2_LV
  N4: U1.GPIO26, Part2.RX_LV
  N5: U1.GPIO27, Part2.TX_LV
  GND: U1.GND, Part1.GND, Part2.GND
  N6: U1.VIN, Part1.HV, Part2.HV
  N7: U1.GPIO16, Part1.TX_LV
  N8: U1.GPIO17, Part1.RX_LV
  N9: U1.GPIO18, Part1.RX2_LV
  N10: U1.GPIO19, Part1.TX2_LV

custom parts:
  ESP32-38PinWide: Generic 38-Pin ESP32 with wide format (only access to one side of pins on a breadboard) based on Stephen Lilley's HiLetgo ESP-WROOM-32 ESP32 ESP-32S Development Board.
